// Logisim project 12 Hour.circ as structural Verilog: 2 circuits, main circuit main
module main (
);

  wire and_2_out, and_3_out, and_5_out, and_6_out, and_7_out, and_8_out, clock_1_out, d_ff_1_q, d_ff_1_qn,
       n7448_decoder_1_a, n7448_decoder_1_b, n7448_decoder_1_c, n7448_decoder_1_d, n7448_decoder_1_e,
       n7448_decoder_1_f, n7448_decoder_1_g, n7448_decoder_2_a, n7448_decoder_2_b, n7448_decoder_2_c,
       n7448_decoder_2_d, n7448_decoder_2_e, n7448_decoder_2_f, n7448_decoder_2_g, n7448_decoder_3_a,
       n7448_decoder_3_b, n7448_decoder_3_c, n7448_decoder_3_d, n7448_decoder_3_e, n7448_decoder_3_f,
       n7448_decoder_3_g, n7448_decoder_4_a, n7448_decoder_4_b, n7448_decoder_4_c, n7448_decoder_4_d,
       n7448_decoder_4_e, n7448_decoder_4_f, n7448_decoder_4_g, n7448_decoder_5_a, n7448_decoder_5_b,
       n7448_decoder_5_c, n7448_decoder_5_d, n7448_decoder_5_e, n7448_decoder_5_f, n7448_decoder_5_g,
       n7448_decoder_6_a, n7448_decoder_6_b, n7448_decoder_6_c, n7448_decoder_6_d, n7448_decoder_6_e,
       n7448_decoder_6_f, n7448_decoder_6_g, n7490_decade_counter_1_p2, n7490_decade_counter_1_p6,
       n7490_decade_counter_1_p7, n7490_decade_counter_1_p8, n7490_decade_counter_2_p2,
       n7490_decade_counter_2_p3, n7490_decade_counter_2_p6, n7490_decade_counter_2_p7,
       n7490_decade_counter_2_p8, n7490_decade_counter_3_p2, n7490_decade_counter_3_p6,
       n7490_decade_counter_3_p7, n7490_decade_counter_3_p8, n7490_decade_counter_4_p2,
       n7490_decade_counter_4_p3, n7490_decade_counter_4_p6, n7490_decade_counter_4_p7,
       n7490_decade_counter_4_p8, n7490_decade_counter_5_p2, n7490_decade_counter_5_p3,
       n7490_decade_counter_5_p6, n7490_decade_counter_5_p7, n7490_decade_counter_5_p8,
       n7490_decade_counter_6_p2, n7490_decade_counter_6_p6, n7490_decade_counter_6_p7,
       n7490_decade_counter_6_p8, not_1_out, not_2_out, not_3_out, not_4_out, not_5_out, not_6_out;

  Clock clock_1 (.out(clock_1_out));
  // _7490__Decade_Counter 7490_decade_counter_1: pin names not known; wires that end beside it: clock_1_out, n7490_decade_counter_1_p2, 1'b0, n7490_decade_counter_1_p2, 1'b0, n7490_decade_counter_1_p6, n7490_decade_counter_1_p7, n7490_decade_counter_1_p8
  _7448_decoder u_7448_decoder_1 (
    .X(n7490_decade_counter_1_p6), .Y(n7490_decade_counter_1_p8), .Z(n7490_decade_counter_1_p7),
    .W(n7490_decade_counter_1_p2), .a(n7448_decoder_1_a), .b(n7448_decoder_1_b), .c(n7448_decoder_1_c),
    .d(n7448_decoder_1_d), .e(n7448_decoder_1_e), .f(n7448_decoder_1_f), .g(n7448_decoder_1_g));
  // _7490__Decade_Counter 7490_decade_counter_2: pin names not known; wires that end beside it: n7490_decade_counter_1_p6, n7490_decade_counter_2_p2, n7490_decade_counter_2_p3, n7490_decade_counter_2_p2, n7490_decade_counter_2_p3, n7490_decade_counter_2_p6, n7490_decade_counter_2_p7, n7490_decade_counter_2_p8
  and and_1 (n7490_decade_counter_2_p3, n7490_decade_counter_2_p7, n7490_decade_counter_2_p8);
  // _7490__Decade_Counter 7490_decade_counter_3: pin names not known; wires that end beside it: n7490_decade_counter_2_p3, n7490_decade_counter_3_p2, 1'b0, n7490_decade_counter_3_p2, 1'b0, n7490_decade_counter_3_p6, n7490_decade_counter_3_p7, n7490_decade_counter_3_p8
  _7448_decoder u_7448_decoder_2 (
    .X(n7490_decade_counter_2_p6), .Y(n7490_decade_counter_2_p8), .Z(n7490_decade_counter_2_p7),
    .W(n7490_decade_counter_2_p2), .a(n7448_decoder_2_a), .b(n7448_decoder_2_b), .c(n7448_decoder_2_c),
    .d(n7448_decoder_2_d), .e(n7448_decoder_2_e), .f(n7448_decoder_2_f), .g(n7448_decoder_2_g));
  _7448_decoder u_7448_decoder_3 (
    .X(n7490_decade_counter_4_p6), .Y(n7490_decade_counter_4_p8), .Z(n7490_decade_counter_4_p7),
    .W(n7490_decade_counter_4_p2), .a(n7448_decoder_3_a), .b(n7448_decoder_3_b), .c(n7448_decoder_3_c),
    .d(n7448_decoder_3_d), .e(n7448_decoder_3_e), .f(n7448_decoder_3_f), .g(n7448_decoder_3_g));
  _7_Segment_Display u_7_segment_display_1 (
    .g(n7448_decoder_4_g), .f(n7448_decoder_4_f), .a(n7448_decoder_4_a), .b(n7448_decoder_4_b),
    .e(n7448_decoder_4_e), .d(n7448_decoder_4_d), .c(n7448_decoder_4_c));  // open: dp
  // _7490__Decade_Counter 7490_decade_counter_4: pin names not known; wires that end beside it: n7490_decade_counter_3_p6, n7490_decade_counter_4_p2, n7490_decade_counter_4_p3, n7490_decade_counter_4_p2, n7490_decade_counter_4_p3, n7490_decade_counter_4_p6, n7490_decade_counter_4_p7, n7490_decade_counter_4_p8
  _7_Segment_Display u_7_segment_display_2 (
    .g(n7448_decoder_2_g), .f(n7448_decoder_2_f), .a(n7448_decoder_2_a), .b(n7448_decoder_2_b),
    .e(n7448_decoder_2_e), .d(n7448_decoder_2_d), .c(n7448_decoder_2_c));  // open: dp
  _7_Segment_Display u_7_segment_display_3 (
    .g(n7448_decoder_3_g), .f(n7448_decoder_3_f), .a(n7448_decoder_3_a), .b(n7448_decoder_3_b),
    .e(n7448_decoder_3_e), .d(n7448_decoder_3_d), .c(n7448_decoder_3_c));  // open: dp
  _7448_decoder u_7448_decoder_4 (
    .X(n7490_decade_counter_6_p6), .Y(n7490_decade_counter_6_p8), .Z(n7490_decade_counter_6_p7),
    .W(n7490_decade_counter_6_p2), .a(n7448_decoder_4_a), .b(n7448_decoder_4_b), .c(n7448_decoder_4_c),
    .d(n7448_decoder_4_d), .e(n7448_decoder_4_e), .f(n7448_decoder_4_f), .g(n7448_decoder_4_g));
  not not_1 (not_1_out, n7490_decade_counter_6_p6);
  not not_2 (not_2_out, n7490_decade_counter_6_p8);
  not not_3 (not_3_out, n7490_decade_counter_6_p7);
  and and_2 (and_2_out, not_1_out, not_2_out);
  and and_3 (and_3_out, not_3_out, n7490_decade_counter_6_p2);
  _7_Segment_Display u_7_segment_display_4 (
    .g(n7448_decoder_1_g), .f(n7448_decoder_1_f), .a(n7448_decoder_1_a), .b(n7448_decoder_1_b),
    .e(n7448_decoder_1_e), .d(n7448_decoder_1_d), .c(n7448_decoder_1_c));  // open: dp
  _7_Segment_Display u_7_segment_display_5 (
    .g(n7448_decoder_5_g), .f(n7448_decoder_5_f), .a(n7448_decoder_5_a), .b(n7448_decoder_5_b),
    .e(n7448_decoder_5_e), .d(n7448_decoder_5_d), .c(n7448_decoder_5_c));  // open: dp
  and and_4 (n7490_decade_counter_4_p3, n7490_decade_counter_4_p7, n7490_decade_counter_4_p8);
  _7_Segment_Display u_7_segment_display_6 (
    .g(n7448_decoder_6_g), .f(n7448_decoder_6_f), .a(n7448_decoder_6_a), .b(n7448_decoder_6_b),
    .e(n7448_decoder_6_e), .d(n7448_decoder_6_d), .c(n7448_decoder_6_c));  // open: dp
  and and_5 (and_5_out, and_2_out, and_3_out);
  _7448_decoder u_7448_decoder_5 (
    .X(n7490_decade_counter_3_p6), .Y(n7490_decade_counter_3_p8), .Z(n7490_decade_counter_3_p7),
    .W(n7490_decade_counter_3_p2), .a(n7448_decoder_5_a), .b(n7448_decoder_5_b), .c(n7448_decoder_5_c),
    .d(n7448_decoder_5_d), .e(n7448_decoder_5_e), .f(n7448_decoder_5_f), .g(n7448_decoder_5_g));
  // _7490__Decade_Counter 7490_decade_counter_5: pin names not known; wires that end beside it: n7490_decade_counter_4_p3, n7490_decade_counter_5_p2, n7490_decade_counter_5_p3, n7490_decade_counter_5_p2, n7490_decade_counter_5_p3, n7490_decade_counter_5_p6, n7490_decade_counter_5_p7, n7490_decade_counter_5_p8
  _7448_decoder u_7448_decoder_6 (
    .X(n7490_decade_counter_5_p6), .Y(n7490_decade_counter_5_p8), .Z(n7490_decade_counter_5_p7),
    .W(n7490_decade_counter_5_p2), .a(n7448_decoder_6_a), .b(n7448_decoder_6_b), .c(n7448_decoder_6_c),
    .d(n7448_decoder_6_d), .e(n7448_decoder_6_e), .f(n7448_decoder_6_f), .g(n7448_decoder_6_g));
  not not_4 (not_4_out, n7490_decade_counter_5_p6);
  not not_5 (not_5_out, n7490_decade_counter_5_p8);
  and and_6 (and_6_out, not_4_out, not_5_out);
  and and_7 (and_7_out, n7490_decade_counter_5_p7, n7490_decade_counter_5_p2);
  and and_8 (and_8_out, and_6_out, and_7_out);
  // _7490__Decade_Counter 7490_decade_counter_6: pin names not known; wires that end beside it: n7490_decade_counter_5_p6, n7490_decade_counter_6_p2, n7490_decade_counter_5_p3, n7490_decade_counter_6_p2, n7490_decade_counter_5_p3, n7490_decade_counter_6_p6, n7490_decade_counter_6_p7, n7490_decade_counter_6_p8
  and and_9 (n7490_decade_counter_5_p3, and_8_out, and_5_out);
  D_Flip_Flop d_ff_1 (
    .clk(n7490_decade_counter_5_p3), .D(d_ff_1_qn), .Q(d_ff_1_q), .Qn(d_ff_1_qn));  // open: preset, en, reset
  _7_Segment_Display u_7_segment_display_7 (
    .g(1'b1), .f(1'b1), .a(1'b1), .b(1'b1), .e(1'b1), .c(not_6_out));  // open: d, dp
  not not_6 (not_6_out, d_ff_1_q);
endmodule

module _7448_decoder (
  input  X,
  input  Y,
  input  Z,
  input  W,
  output a,
  output b,
  output c,
  output d,
  output e,
  output f,
  output g
);

  wire and_1_out, and_2_out, and_3_out, and_4_out, and_5_out, and_6_out, and_7_out, and_8_out, and_9_out,
       and_10_out, and_11_out, and_12_out, and_13_out, and_14_out, and_15_out, and_16_out, and_17_out,
       and_18_out, not_1_out, not_2_out, not_3_out, not_4_out, not_5_out, not_6_out, not_7_out, not_8_out,
       not_9_out, not_10_out, not_11_out, not_12_out, not_13_out, not_14_out, not_15_out, not_16_out,
       not_17_out, not_18_out, not_19_out, not_20_out, not_21_out, or_1_out, or_2_out, or_3_out, or_4_out,
       or_5_out, or_7_out, or_8_out, or_9_out, or_10_out, or_11_out, or_12_out, or_15_out, or_16_out;

  not not_1 (not_1_out, Y);
  and and_1 (and_1_out, not_1_out, not_2_out);
  not not_2 (not_2_out, W);
  and and_2 (and_2_out, Y, W);
  not not_3 (not_3_out, Y);
  not not_4 (not_4_out, Z);
  and and_3 (and_3_out, not_4_out, not_5_out);
  not not_5 (not_5_out, W);
  not not_6 (not_6_out, Z);
  or or_1 (or_1_out, not_6_out, W);
  or or_2 (or_2_out, Y, X);
  not not_7 (not_7_out, Y);
  and and_4 (and_4_out, not_7_out, not_8_out);
  not not_8 (not_8_out, W);
  not not_9 (not_9_out, Y);
  and and_5 (and_5_out, not_9_out, Z);
  not not_10 (not_10_out, W);
  and and_6 (and_6_out, Y, not_11_out);
  not not_11 (not_11_out, Z);
  not not_12 (not_12_out, Y);
  and and_7 (and_7_out, not_12_out, not_13_out);
  not not_13 (not_13_out, W);
  and and_8 (and_8_out, Z, not_14_out);
  not not_14 (not_14_out, W);
  not not_15 (not_15_out, Z);
  and and_9 (and_9_out, not_15_out, not_16_out);
  not not_16 (not_16_out, W);
  and and_10 (and_10_out, Y, not_17_out);
  not not_17 (not_17_out, Z);
  and and_11 (and_11_out, Y, not_18_out);
  not not_18 (not_18_out, W);
  not not_19 (not_19_out, Y);
  and and_12 (and_12_out, not_19_out, Z);
  and and_13 (and_13_out, Y, not_20_out);
  not not_20 (not_20_out, Z);
  and and_14 (and_14_out, Y, not_21_out);
  not not_21 (not_21_out, W);
  or or_3 (or_3_out, and_1_out, Z);
  or or_4 (or_4_out, and_2_out, X);
  or or_5 (or_5_out, not_3_out, and_3_out);
  and and_15 (and_15_out, Z, W);
  or or_6 (c, or_1_out, or_2_out);
  or or_7 (or_7_out, and_4_out, and_5_out);
  and and_16 (and_16_out, Z, not_10_out);
  and and_17 (and_17_out, and_6_out, W);
  or or_8 (or_8_out, and_7_out, and_8_out);
  and and_18 (and_18_out, X, Y);
  or or_9 (or_9_out, and_9_out, and_10_out);
  or or_10 (or_10_out, and_11_out, X);
  or or_11 (or_11_out, and_12_out, and_13_out);
  or or_12 (or_12_out, and_14_out, X);
  or or_13 (a, or_3_out, or_4_out);
  or or_14 (b, or_5_out, and_15_out);
  or or_15 (or_15_out, or_7_out, and_16_out);
  or or_16 (or_16_out, and_17_out, X);
  or or_17 (e, or_8_out, and_18_out);
  or or_18 (f, or_9_out, or_10_out);
  or or_19 (g, or_11_out, or_12_out);
  or or_20 (d, or_15_out, or_16_out);
endmodule
