// Logisim project ALL FUNC.circ as structural Verilog: 3 circuits, main circuit main
module main (
  input  in_1,
  input  A4,
  input  A3,
  input  A2,
  input  A1,
  input  B4,
  input  B3,
  input  B2,
  input  B1,
  input  in_10,
  input  in_11
);

  wire and_1_out, and_2_out, m_1_c0, m_1_c1, m_1_c2, m_1_c3, main_1_out_9, main_1_out_10, main_1_out_11,
       main_1_out_12, main_1_out_13, main_2_out_9, main_2_out_10, main_2_out_11, main_2_out_12, n4x1_mux_2_o,
       n4x1_mux_3_o, n4x1_mux_4_o, n4x1_mux_5_o, n7448_decoder_1_a, n7448_decoder_1_b, n7448_decoder_1_c,
       n7448_decoder_1_d, n7448_decoder_1_e, n7448_decoder_1_f, n7448_decoder_1_g,
       n7483_4_bit_binary_full_adders_with_fast_carry_1_p2,
       n7483_4_bit_binary_full_adders_with_fast_carry_1_p6,
       n7483_4_bit_binary_full_adders_with_fast_carry_1_p10,
       n7483_4_bit_binary_full_adders_with_fast_carry_1_p11,
       n7483_4_bit_binary_full_adders_with_fast_carry_1_p16, or_1_out, xor_1_out;

  ADDERSUBTRACTOR__3__main main_1 (
    .A4(A4), .A3(A3), .A2(A2), .A1(A1), .B4(B4), .B3(B3), .B2(B2), .B1(B1), .out_9(main_1_out_9),
    .out_10(main_1_out_10), .out_11(main_1_out_11), .out_12(main_1_out_12), .out_13(main_1_out_13));  // open: out_14
  xor xor_1 (xor_1_out, or_1_out, in_10);
  or or_1 (or_1_out, and_2_out, and_1_out);
  and and_1 (and_1_out, main_1_out_10, main_1_out_12);
  and and_2 (and_2_out, main_1_out_10, main_1_out_11);
  // _7483___4_bit_Binary_Full_Adders_with_Fast_Carry 7483_4_bit_binary_full_adders_with_fast_carry_1: pin names not known; wires that end beside it: main_1_out_10, n7483_4_bit_binary_full_adders_with_fast_carry_1_p2, main_1_out_11, xor_1_out, 1'b1, n7483_4_bit_binary_full_adders_with_fast_carry_1_p6, xor_1_out, main_1_out_12, in_1, n7483_4_bit_binary_full_adders_with_fast_carry_1_p10, n7483_4_bit_binary_full_adders_with_fast_carry_1_p11, 1'b0, 1'b0, 1'b0, main_1_out_13, n7483_4_bit_binary_full_adders_with_fast_carry_1_p16
  M m_1 (
    .B0(B1), .B1(B2), .B2(B3), .C0(m_1_c0), .C1(m_1_c1), .C2(m_1_c2), .C3(m_1_c3), .A0(A1), .A1(A2), .A2(A3),
    .A3(A4), .B3(B4));  // open: out_13, out_14, out_15
  FINAL_DIVISION_2_main main_2 (
    .A4(A4), .A3(A3), .A2(A2), .A1(A1), .B4(B4), .B3(B3), .B2(B2), .B1(B1), .out_9(main_2_out_9),
    .out_10(main_2_out_10), .out_11(main_2_out_11), .out_12(main_2_out_12));
  _4x1_MUX u_4x1_mux_1 (
    .S1(in_10), .S0(in_11), .I0(n7483_4_bit_binary_full_adders_with_fast_carry_1_p10));  // open: I1, I2, I3, O
  _4x1_MUX u_4x1_mux_2 (
    .S1(in_10), .S0(in_11), .I0(main_1_out_9), .I1(main_1_out_9), .I2(m_1_c3), .I3(main_2_out_9),
    .O(n4x1_mux_2_o));
  _4x1_MUX u_4x1_mux_3 (
    .S1(in_10), .S0(in_11), .I0(n7483_4_bit_binary_full_adders_with_fast_carry_1_p2),
    .I1(n7483_4_bit_binary_full_adders_with_fast_carry_1_p2), .I2(m_1_c2), .I3(main_2_out_10),
    .O(n4x1_mux_3_o));
  _4x1_MUX u_4x1_mux_4 (
    .S1(in_10), .S0(in_11), .I0(n7483_4_bit_binary_full_adders_with_fast_carry_1_p6),
    .I1(n7483_4_bit_binary_full_adders_with_fast_carry_1_p6), .I2(m_1_c1), .I3(main_2_out_11),
    .O(n4x1_mux_4_o));
  _4x1_MUX u_4x1_mux_5 (
    .S1(in_10), .S0(in_11), .I0(n7483_4_bit_binary_full_adders_with_fast_carry_1_p16),
    .I1(n7483_4_bit_binary_full_adders_with_fast_carry_1_p16), .I2(m_1_c0), .I3(main_2_out_12),
    .O(n4x1_mux_5_o));
  _7448_decoder u_7448_decoder_1 (
    .X(1'b0), .Y(n4x1_mux_3_o), .Z(n4x1_mux_4_o), .W(n4x1_mux_5_o), .a(n7448_decoder_1_a),
    .b(n7448_decoder_1_b), .c(n7448_decoder_1_c), .d(n7448_decoder_1_d), .e(n7448_decoder_1_e),
    .f(n7448_decoder_1_f), .g(n7448_decoder_1_g));
  _7_Segment_Display u_7_segment_display_1 (.g(n4x1_mux_2_o));  // open: f, a, b, e, d, c, dp
  _7_Segment_Display u_7_segment_display_2 (
    .f(n7483_4_bit_binary_full_adders_with_fast_carry_1_p11),
    .e(n7483_4_bit_binary_full_adders_with_fast_carry_1_p11));  // open: g, a, b, d, c, dp
  _7_Segment_Display u_7_segment_display_3 (
    .g(n7448_decoder_1_g), .f(n7448_decoder_1_f), .a(n7448_decoder_1_a), .b(n7448_decoder_1_b),
    .e(n7448_decoder_1_e), .d(n7448_decoder_1_d), .c(n7448_decoder_1_c));  // open: dp
endmodule

module _7448_decoder (
  input  X,
  input  Y,
  input  Z,
  input  W,
  output a,
  output b,
  output c,
  output d,
  output e,
  output f,
  output g
);

  wire and_1_out, and_2_out, and_3_out, and_4_out, and_5_out, and_6_out, and_7_out, and_8_out, and_9_out,
       and_10_out, and_11_out, and_12_out, and_13_out, and_14_out, and_15_out, and_16_out, and_17_out,
       not_1_out, not_2_out, not_3_out, not_4_out, not_5_out, not_6_out, not_7_out, not_8_out, not_9_out,
       not_10_out, not_11_out, not_12_out, not_13_out, not_14_out, not_15_out, not_16_out, not_17_out,
       not_18_out, not_19_out, not_20_out, not_21_out, or_1_out, or_2_out, or_3_out, or_4_out, or_6_out,
       or_8_out, or_9_out, or_10_out, or_11_out, or_14_out, or_15_out;

  not not_1 (not_1_out, Y);
  and and_1 (and_1_out, not_1_out, not_2_out);
  not not_2 (not_2_out, W);
  and and_2 (and_2_out, Y, W);
  not not_3 (not_3_out, Y);
  not not_4 (not_4_out, Z);
  and and_3 (and_3_out, not_4_out, not_5_out);
  not not_5 (not_5_out, W);
  not not_6 (not_6_out, Z);
  or or_1 (or_1_out, not_6_out, W);
  not not_7 (not_7_out, Y);
  and and_4 (and_4_out, not_7_out, not_8_out);
  not not_8 (not_8_out, W);
  not not_9 (not_9_out, Y);
  and and_5 (and_5_out, not_9_out, Z);
  not not_10 (not_10_out, W);
  and and_6 (and_6_out, Y, not_11_out);
  not not_11 (not_11_out, Z);
  not not_12 (not_12_out, Y);
  and and_7 (and_7_out, not_12_out, not_13_out);
  not not_13 (not_13_out, W);
  and and_8 (and_8_out, Z, not_14_out);
  not not_14 (not_14_out, W);
  not not_15 (not_15_out, Z);
  and and_9 (and_9_out, not_15_out, not_16_out);
  not not_16 (not_16_out, W);
  and and_10 (and_10_out, Y, not_17_out);
  not not_17 (not_17_out, Z);
  and and_11 (and_11_out, Y, not_18_out);
  not not_18 (not_18_out, W);
  not not_19 (not_19_out, Y);
  and and_12 (and_12_out, not_19_out, Z);
  and and_13 (and_13_out, Y, not_20_out);
  not not_20 (not_20_out, Z);
  and and_14 (and_14_out, Y, not_21_out);
  not not_21 (not_21_out, W);
  or or_2 (or_2_out, and_1_out, Z);
  or or_3 (or_3_out, and_2_out, X);
  or or_4 (or_4_out, not_3_out, and_3_out);
  and and_15 (and_15_out, Z, W);
  or or_5 (c, or_1_out, Y);
  or or_6 (or_6_out, and_4_out, and_5_out);
  and and_16 (and_16_out, Z, not_10_out);
  and and_17 (and_17_out, and_6_out, W);
  or or_7 (e, and_7_out, and_8_out);
  or or_8 (or_8_out, and_9_out, and_10_out);
  or or_9 (or_9_out, and_11_out, X);
  or or_10 (or_10_out, and_12_out, and_13_out);
  or or_11 (or_11_out, and_14_out, X);
  or or_12 (a, or_2_out, or_3_out);
  or or_13 (b, or_4_out, and_15_out);
  or or_14 (or_14_out, or_6_out, and_16_out);
  or or_15 (or_15_out, and_17_out, X);
  or or_16 (f, or_8_out, or_9_out);
  or or_17 (g, or_10_out, or_11_out);
  or or_18 (d, or_14_out, or_15_out);
endmodule

module M (
  input  A0,
  input  A1,
  input  A2,
  input  A3,
  input  B3,
  input  B0,
  input  B1,
  input  B2,
  output C0,
  output C1,
  output C2,
  output C3,
  output out_13,
  output out_14,
  output out_15
);

  wire adder_1_cout, adder_2_cout, adder_2_out, adder_3_cout, adder_3_out, adder_4_cout, adder_5_cout,
       and_2_out, and_3_out, and_4_out, and_5_out, and_6_out, and_7_out, and_8_out, and_9_out;

  and and_1 (C0, B0, A0);
  and and_2 (and_2_out, B1, A0);
  and and_3 (and_3_out, B2, A0);
  and and_4 (and_4_out, B0, A1);
  and and_5 (and_5_out, B1, A1);
  and and_6 (and_6_out, B2, A1);
  Adder #(.width(1)) adder_1 (.a(and_4_out), .b(and_2_out), .out(C1), .cin(1'b0), .cout(adder_1_cout));
  Adder #(.width(1)) adder_2 (.a(and_5_out), .b(and_3_out), .out(adder_2_out), .cin(adder_1_cout), .cout(adder_2_cout));
  Adder #(.width(1)) adder_3 (.a(and_6_out), .b(1'b0), .out(adder_3_out), .cin(adder_2_cout), .cout(adder_3_cout));
  and and_7 (and_7_out, B0, A2);
  and and_8 (and_8_out, B1, A2);
  and and_9 (and_9_out, B2, A2);
  Adder #(.width(1)) adder_4 (.a(and_7_out), .b(adder_2_out), .out(C2), .cin(1'b0), .cout(adder_4_cout));
  Adder #(.width(1)) adder_5 (.a(and_8_out), .b(adder_3_out), .out(out_13), .cin(adder_4_cout), .cout(adder_5_cout));
  Adder #(.width(1)) adder_6 (.a(and_9_out), .b(adder_3_cout), .out(out_14), .cin(adder_5_cout), .cout(out_15));
  xor xor_1 (C3, A3, B3);
endmodule
