// Logisim project 7448 Decoder (2).circ as structural Verilog: 2 circuits, main circuit main
module main (
  input  A0,
  input  A1,
  input  A2,
  input  A3,
  input  B0,
  input  B1,
  input  B2,
  input  B3,
  output DIFF0,
  output DIFF1,
  output DIFF2,
  output DIFF3,
  output BORROW
);

  wire adder_1_cout, adder_2_cout, adder_3_cout, not_1_out, not_2_out, not_3_out, not_4_out;

  not not_1 (not_1_out, B0);
  not not_2 (not_2_out, B1);
  not not_3 (not_3_out, B2);
  not not_4 (not_4_out, B3);
  Adder #(.width(1)) adder_1 (.a(A0), .b(not_1_out), .out(DIFF0), .cin(1'b1), .cout(adder_1_cout));
  Adder #(.width(1)) adder_2 (.a(A1), .b(not_2_out), .out(DIFF1), .cin(adder_1_cout), .cout(adder_2_cout));
  Adder #(.width(1)) adder_3 (.a(A2), .b(not_3_out), .out(DIFF2), .cin(adder_2_cout), .cout(adder_3_cout));
  Adder #(.width(1)) adder_4 (.a(A3), .b(not_4_out), .out(DIFF3), .cin(adder_3_cout), .cout(BORROW));
endmodule

module _7448_decoder (
  input  X,
  input  Y,
  input  Z,
  input  W,
  output a,
  output b,
  output c,
  output d,
  output e,
  output f,
  output g
);

  wire and_1_out, and_2_out, and_3_out, and_4_out, and_5_out, and_6_out, and_7_out, and_8_out, and_9_out,
       and_10_out, and_11_out, and_12_out, and_13_out, and_14_out, and_15_out, not_1_out, not_2_out,
       not_3_out, not_4_out, not_5_out, not_6_out, not_7_out, not_8_out, not_9_out, not_10_out, not_11_out,
       not_12_out, not_13_out, not_14_out, not_15_out, not_16_out, not_17_out, not_18_out, not_19_out,
       not_20_out;

  not not_1 (not_1_out, Y);
  and and_1 (and_1_out, not_1_out, not_2_out);
  not not_2 (not_2_out, W);
  and and_2 (and_2_out, Y, W);
  not not_3 (not_3_out, Y);
  not not_4 (not_4_out, Z);
  and and_3 (and_3_out, not_4_out, not_5_out);
  not not_5 (not_5_out, W);
  and and_4 (and_4_out, Z, W);
  not not_6 (not_6_out, Z);
  or or_1 (c, not_6_out, W, Y);
  not not_7 (not_7_out, Y);
  and and_5 (and_5_out, not_7_out, not_8_out);
  not not_8 (not_8_out, W);
  not not_9 (not_9_out, Y);
  and and_6 (and_6_out, not_9_out, Z);
  and and_7 (and_7_out, Z, not_10_out);
  not not_10 (not_10_out, W);
  and and_8 (and_8_out, Y, not_11_out, W);
  not not_11 (not_11_out, Z);
  not not_12 (not_12_out, Y);
  and and_9 (and_9_out, not_12_out, not_13_out);
  not not_13 (not_13_out, W);
  and and_10 (and_10_out, Z, not_14_out);
  not not_14 (not_14_out, W);
  not not_15 (not_15_out, Z);
  and and_11 (and_11_out, not_15_out, not_16_out);
  not not_16 (not_16_out, W);
  and and_12 (and_12_out, Y, not_17_out);
  not not_17 (not_17_out, Z);
  and and_13 (and_13_out, Y, not_18_out);
  not not_18 (not_18_out, W);
  and and_14 (and_14_out, Z, not_19_out);
  not not_19 (not_19_out, W);
  and and_15 (and_15_out, Y, not_20_out);
  not not_20 (not_20_out, Z);
  or or_2 (a, and_1_out, Z, and_2_out, X);
  or or_3 (b, not_3_out, and_3_out, and_4_out);
  or or_4 (d, and_5_out, and_6_out, and_7_out, and_8_out, X);
  or or_5 (e, and_9_out, and_10_out);
  or or_6 (f, and_11_out, and_12_out, and_13_out, X);
  or or_7 (g, and_14_out, and_15_out, X);
endmodule
