// Logisim project ADDERSUBTRACTOR (3).circ as structural Verilog: 1 circuit, main circuit main
module main (
  input  A4,
  input  A3,
  input  A2,
  input  A1,
  input  B4,
  input  B3,
  input  B2,
  input  B1,
  output out_9,
  output out_10,
  output out_11,
  output out_12,
  output out_13,
  output out_14
);

  wire n7483_4_bit_binary_full_adders_with_fast_carry_1_p3,
       n7483_4_bit_binary_full_adders_with_fast_carry_1_p4,
       n7483_4_bit_binary_full_adders_with_fast_carry_1_p5,
       n7483_4_bit_binary_full_adders_with_fast_carry_1_p12,
       n7483_4_bit_binary_full_adders_with_fast_carry_1_p15,
       n7483_4_bit_binary_full_adders_with_fast_carry_2_p3,
       n7483_4_bit_binary_full_adders_with_fast_carry_3_p3,
       n7483_4_bit_binary_full_adders_with_fast_carry_3_p4,
       n7483_4_bit_binary_full_adders_with_fast_carry_3_p11,
       n7483_4_bit_binary_full_adders_with_fast_carry_3_p14, xor_1_out, xor_2_out, xor_3_out, xor_4_out,
       xor_5_out, xor_6_out, xor_7_out, xor_8_out, xor_9_out, xor_11_out, xor_12_out, xor_13_out, xor_14_out;

  xor xor_1 (xor_1_out, A4, B4);
  xor xor_2 (xor_2_out, A4, A3);
  xor xor_3 (xor_3_out, A4, A2);
  xor xor_4 (xor_4_out, A4, A1);
  xor xor_5 (xor_5_out, B4, B3);
  xor xor_6 (xor_6_out, B4, B2);
  xor xor_7 (xor_7_out, B4, B1);
  xor xor_8 (xor_8_out, B4, 1'b0);
  xor xor_9 (xor_9_out, A4, 1'b0);
  // _7483___4_bit_Binary_Full_Adders_with_Fast_Carry 7483_4_bit_binary_full_adders_with_fast_carry_1: pin names not known; wires that end beside it: xor_8_out, xor_9_out, n7483_4_bit_binary_full_adders_with_fast_carry_1_p3, n7483_4_bit_binary_full_adders_with_fast_carry_1_p4, n7483_4_bit_binary_full_adders_with_fast_carry_1_p5, xor_2_out, 1'b0, xor_5_out, 1'b0, 1'b1, xor_7_out, n7483_4_bit_binary_full_adders_with_fast_carry_1_p12, xor_4_out, xor_6_out, n7483_4_bit_binary_full_adders_with_fast_carry_1_p15, xor_3_out
  // _7483___4_bit_Binary_Full_Adders_with_Fast_Carry 7483_4_bit_binary_full_adders_with_fast_carry_2: pin names not known; wires that end beside it: 1'b0, xor_9_out, n7483_4_bit_binary_full_adders_with_fast_carry_2_p3, xor_2_out, 1'b0, 1'b0, 1'b0, 1'b0, 1'b1, 1'b0, 1'b0, 1'b0, 1'b0
  // _7483___4_bit_Binary_Full_Adders_with_Fast_Carry 7483_4_bit_binary_full_adders_with_fast_carry_3: pin names not known; wires that end beside it: 1'b0, n7483_4_bit_binary_full_adders_with_fast_carry_1_p3, n7483_4_bit_binary_full_adders_with_fast_carry_3_p3, n7483_4_bit_binary_full_adders_with_fast_carry_3_p4, n7483_4_bit_binary_full_adders_with_fast_carry_1_p4, B4, 1'b0, 1'b0, 1'b1, A4, n7483_4_bit_binary_full_adders_with_fast_carry_3_p11, n7483_4_bit_binary_full_adders_with_fast_carry_1_p15, 1'b0, n7483_4_bit_binary_full_adders_with_fast_carry_3_p14, n7483_4_bit_binary_full_adders_with_fast_carry_1_p12
  _2x1_MUX u_2x1_mux_1 (
    .S0(xor_1_out), .I0(n7483_4_bit_binary_full_adders_with_fast_carry_1_p5),
    .I1(n7483_4_bit_binary_full_adders_with_fast_carry_3_p3), .O(out_9));
  xor xor_10 (out_14, n7483_4_bit_binary_full_adders_with_fast_carry_2_p3, n7483_4_bit_binary_full_adders_with_fast_carry_1_p5);
  xor xor_11 (xor_11_out, out_9, n7483_4_bit_binary_full_adders_with_fast_carry_3_p3);
  xor xor_12 (xor_12_out, out_9, n7483_4_bit_binary_full_adders_with_fast_carry_3_p4);
  xor xor_13 (xor_13_out, out_9, n7483_4_bit_binary_full_adders_with_fast_carry_3_p11);
  xor xor_14 (xor_14_out, out_9, n7483_4_bit_binary_full_adders_with_fast_carry_3_p14);
  // _7483___4_bit_Binary_Full_Adders_with_Fast_Carry 7483_4_bit_binary_full_adders_with_fast_carry_4: pin names not known; wires that end beside it: 1'b0, xor_11_out, out_10, out_11, xor_12_out, out_9, 1'b0, 1'b0, out_12, xor_14_out, 1'b0, out_13, xor_13_out
endmodule
