// Logisim project ADDERSUBTRACTORFinal.circ as structural Verilog: 1 circuit, main circuit main
module main (
  input  A4,
  input  A3,
  input  A2,
  input  A1,
  input  B4,
  input  B3,
  input  B2,
  input  B1,
  output SIGN,
  output _4,
  output _2,
  output _1,
  output Overflow
);

  wire and_1_out, and_2_out, and_3_out, and_4_out, and_5_out, and_6_out, and_7_out, and_8_out,
       n7483_4_bit_binary_full_adders_with_fast_carry_1_p3,
       n7483_4_bit_binary_full_adders_with_fast_carry_1_p4,
       n7483_4_bit_binary_full_adders_with_fast_carry_1_p11,
       n7483_4_bit_binary_full_adders_with_fast_carry_1_p14,
       n7483_4_bit_binary_full_adders_with_fast_carry_2_p3,
       n7483_4_bit_binary_full_adders_with_fast_carry_2_p4,
       n7483_4_bit_binary_full_adders_with_fast_carry_2_p11,
       n7483_4_bit_binary_full_adders_with_fast_carry_2_p14, not_1_out, not_2_out, not_3_out, not_4_out,
       or_1_out, or_2_out, xor_1_out, xor_2_out, xor_3_out, xor_4_out, xor_5_out, xor_6_out, xor_7_out,
       xor_8_out, xor_9_out, xor_10_out, xor_11_out, xor_12_out;

  xor xor_1 (xor_1_out, A4, A3);
  xor xor_2 (xor_2_out, A4, A2);
  xor xor_3 (xor_3_out, A4, A1);
  xor xor_4 (xor_4_out, B4, B3);
  xor xor_5 (xor_5_out, B4, B2);
  xor xor_6 (xor_6_out, B4, B1);
  // _7483___4_bit_Binary_Full_Adders_with_Fast_Carry 7483_4_bit_binary_full_adders_with_fast_carry_1: pin names not known; wires that end beside it: B4, A4, n7483_4_bit_binary_full_adders_with_fast_carry_1_p3, n7483_4_bit_binary_full_adders_with_fast_carry_1_p4, xor_1_out, 1'b0, xor_4_out, 1'b0, 1'b1, xor_6_out, n7483_4_bit_binary_full_adders_with_fast_carry_1_p11, xor_3_out, xor_5_out, n7483_4_bit_binary_full_adders_with_fast_carry_1_p14, xor_2_out
  not not_1 (not_1_out, A4);
  not not_2 (not_2_out, B4);
  // _7483___4_bit_Binary_Full_Adders_with_Fast_Carry 7483_4_bit_binary_full_adders_with_fast_carry_2: pin names not known; wires that end beside it: 1'b0, n7483_4_bit_binary_full_adders_with_fast_carry_1_p3, n7483_4_bit_binary_full_adders_with_fast_carry_2_p3, n7483_4_bit_binary_full_adders_with_fast_carry_2_p4, n7483_4_bit_binary_full_adders_with_fast_carry_1_p4, B4, 1'b0, 1'b0, 1'b1, A4, n7483_4_bit_binary_full_adders_with_fast_carry_2_p11, n7483_4_bit_binary_full_adders_with_fast_carry_1_p14, 1'b0, n7483_4_bit_binary_full_adders_with_fast_carry_2_p14, n7483_4_bit_binary_full_adders_with_fast_carry_1_p11
  and and_1 (and_1_out, not_1_out, not_2_out);
  not not_3 (not_3_out, SIGN);
  and and_2 (and_2_out, and_1_out, SIGN);
  and and_3 (and_3_out, A4, B4);
  and and_4 (and_4_out, and_3_out, not_3_out);
  xor xor_7 (xor_7_out, n7483_4_bit_binary_full_adders_with_fast_carry_2_p3, n7483_4_bit_binary_full_adders_with_fast_carry_2_p4);
  xor xor_8 (xor_8_out, n7483_4_bit_binary_full_adders_with_fast_carry_2_p3, n7483_4_bit_binary_full_adders_with_fast_carry_2_p11);
  xor xor_9 (xor_9_out, n7483_4_bit_binary_full_adders_with_fast_carry_2_p3, n7483_4_bit_binary_full_adders_with_fast_carry_2_p14);
  // _7483___4_bit_Binary_Full_Adders_with_Fast_Carry 7483_4_bit_binary_full_adders_with_fast_carry_3: pin names not known; wires that end beside it: 1'b0, n7483_4_bit_binary_full_adders_with_fast_carry_2_p3, SIGN, _4, xor_7_out, n7483_4_bit_binary_full_adders_with_fast_carry_2_p3, 1'b0, 1'b0, 1'b0, _2, xor_9_out, 1'b0, _1, xor_8_out
  xor xor_10 (xor_10_out, n7483_4_bit_binary_full_adders_with_fast_carry_2_p3, n7483_4_bit_binary_full_adders_with_fast_carry_2_p4);
  xor xor_11 (xor_11_out, n7483_4_bit_binary_full_adders_with_fast_carry_2_p3, n7483_4_bit_binary_full_adders_with_fast_carry_2_p11);
  xor xor_12 (xor_12_out, n7483_4_bit_binary_full_adders_with_fast_carry_2_p3, n7483_4_bit_binary_full_adders_with_fast_carry_2_p14);
  or or_1 (or_1_out, and_2_out, and_4_out);
  and and_5 (and_5_out, xor_10_out, xor_11_out);
  and and_6 (and_6_out, and_5_out, xor_12_out);
  or or_2 (or_2_out, or_1_out, and_6_out);
  and and_7 (and_7_out, n7483_4_bit_binary_full_adders_with_fast_carry_2_p4, n7483_4_bit_binary_full_adders_with_fast_carry_2_p11);
  and and_8 (and_8_out, and_7_out, n7483_4_bit_binary_full_adders_with_fast_carry_2_p14);
  not not_4 (not_4_out, and_8_out);
  and and_9 (Overflow, or_2_out, not_4_out);
endmodule
