// Logisim project FINAL DIVISION.circ as structural Verilog: 7 circuits, main circuit main
// B3
module main (
  input  A3,
  input  A2,
  input  A1,
  input  A0,
  input  B3,
  input  B2,
  input  B1,
  input  B0,
  output Q3,
  output Q2,
  output Q1,
  output Q0,
  output ERROR,
  output ZERO_FLAG
);

  wire n2x1_mux_2_o, n2x1_mux_3_o, n2x1_mux_4_o, n2x1_mux_5_o, n2x1_mux_7_o, n2x1_mux_8_o, n2x1_mux_9_o,
       n2x1_mux_10_o, n4_bit_comparator_1_p10, n4_bit_comparator_1_p11, n4_bit_comparator_2_p11,
       n4_bit_comparator_2_p12, n4_bit_comparator_3_a_b_2, n4_bit_comparator_3_a_b_3, or_1_out, or_2_out,
       or_3_out, or_4_out, or_5_out, or_6_out, subtractor_1_a1, subtractor_1_a2, subtractor_1_a4,
       subtractor_1_a8, subtractor_2_a1, subtractor_2_a2, subtractor_2_a4, subtractor_2_a8;

  or or_1 (or_1_out, B0, B1);
  or or_2 (or_2_out, B2, 1'b0);
  nor nor_1 (ERROR, or_1_out, or_2_out);
  // _4_bit_comparator 4_bit_comparator_1: pin names not known; wires that end beside it: B3, 1'b0, 1'b0, 1'b0, A2, 1'b0, B2, B1, B0, n4_bit_comparator_1_p10, n4_bit_comparator_1_p11
  or or_3 (or_3_out, n4_bit_comparator_1_p10, n4_bit_comparator_1_p11);
  xor xor_1 (Q3, A3, B3);
  or or_4 (or_4_out, Q2, Q1);
  or or_5 (or_5_out, Q0, 1'b0);
  nor nor_2 (ZERO_FLAG, or_4_out, or_5_out);
  _2x1_MUX u_2x1_mux_1 (.S0(or_3_out), .I0(1'b0), .I1(1'b1), .O(Q2));
  _2x1_MUX u_2x1_mux_2 (.S0(Q2), .I0(1'b0), .I1(B0), .O(n2x1_mux_2_o));
  _2x1_MUX u_2x1_mux_3 (.S0(Q2), .I0(1'b0), .I1(B1), .O(n2x1_mux_3_o));
  _2x1_MUX u_2x1_mux_4 (.S0(Q2), .I0(1'b0), .I1(B2), .O(n2x1_mux_4_o));
  _2x1_MUX u_2x1_mux_5 (.S0(Q2), .I0(1'b0), .I1(B3), .O(n2x1_mux_5_o));
  Subtractor subtractor_1 (
    .in_1(A2), .in_2(n2x1_mux_2_o), .in_3(A3), .in_4(n2x1_mux_3_o), .in_5(1'b0), .in_6(n2x1_mux_4_o),
    .in_7(1'b0), .in_8(1'b0), .A1(subtractor_1_a1), .A2(subtractor_1_a2), .A4(subtractor_1_a4),
    .A8(subtractor_1_a8));
  // _4_bit_comparator 4_bit_comparator_2: pin names not known; wires that end beside it: subtractor_1_a2, B3, subtractor_1_a4, 1'b0, subtractor_1_a1, A1, 1'b0, B2, B1, B0, n4_bit_comparator_2_p11, n4_bit_comparator_2_p12
  or or_6 (or_6_out, n4_bit_comparator_2_p11, n4_bit_comparator_2_p12);
  _2x1_MUX u_2x1_mux_6 (.S0(or_6_out), .I0(1'b0), .I1(1'b1), .O(Q1));
  Subtractor subtractor_2 (
    .in_1(A1), .in_2(n2x1_mux_7_o), .in_3(subtractor_1_a1), .in_4(n2x1_mux_8_o), .in_5(subtractor_1_a2),
    .in_6(n2x1_mux_9_o), .in_7(subtractor_1_a4), .in_8(1'b0), .A1(subtractor_2_a1), .A2(subtractor_2_a2),
    .A4(subtractor_2_a4), .A8(subtractor_2_a8));
  _2x1_MUX u_2x1_mux_7 (.S0(Q1), .I0(1'b0), .I1(B0), .O(n2x1_mux_7_o));
  _2x1_MUX u_2x1_mux_8 (.S0(Q1), .I0(1'b0), .I1(B1), .O(n2x1_mux_8_o));
  _2x1_MUX u_2x1_mux_9 (.S0(Q1), .I0(1'b0), .I1(B2), .O(n2x1_mux_9_o));
  _2x1_MUX u_2x1_mux_10 (.S0(Q1), .I0(1'b0), .I1(B3), .O(n2x1_mux_10_o));
  _4_bit_comparator u_4_bit_comparator_3 (
    .A3(1'b0), .B3(1'b0), .A2(subtractor_2_a2), .B2(B2), .A1(subtractor_2_a1), .B1(B1), .A0(A0), .B0(B0),
    .A_B_2(n4_bit_comparator_3_a_b_2), .A_B_3(n4_bit_comparator_3_a_b_3));  // open: A_B
  or or_7 (Q0, n4_bit_comparator_3_a_b_2, n4_bit_comparator_3_a_b_3);

  // Notes on the sheet:
  //   0
  //   0
  //   A3
  //   A2
  //   0
  //   A3
  //   A2
  //   A1
endmodule

module _2x1_MUX (
  input  S0,
  input  I0,
  input  I1,
  output O
);

  wire and_1_out, and_2_out, not_1_out;

  not not_1 (not_1_out, S0);
  and and_1 (and_1_out, not_1_out, I0);
  and and_2 (and_2_out, S0, I1);
  or or_1 (O, and_1_out, and_2_out);
endmodule

module _4_bit_comparator (
  input  A3,
  input  B3,
  input  A2,
  input  B2,
  input  A1,
  input  B1,
  input  A0,
  input  B0,
  output A_B,
  output A_B_2,
  output A_B_3
);

  wire and_1_out, and_2_out, and_3_out, and_4_out, and_5_out, and_6_out, and_7_out, and_8_out, and_9_out,
       and_10_out, and_11_out, and_12_out, and_13_out, and_14_out, nor_1_out, nor_2_out, nor_3_out,
       nor_4_out, not_1_out, not_2_out, not_3_out, not_4_out, not_5_out, not_6_out, not_7_out, not_8_out;

  not not_1 (not_1_out, A3);
  not not_2 (not_2_out, B3);
  not not_3 (not_3_out, A2);
  not not_4 (not_4_out, B2);
  not not_5 (not_5_out, A1);
  not not_6 (not_6_out, B1);
  not not_7 (not_7_out, A0);
  not not_8 (not_8_out, B0);
  and and_1 (and_1_out, not_1_out, B3);
  and and_2 (and_2_out, A3, not_2_out);
  and and_3 (and_3_out, not_3_out, B2);
  and and_4 (and_4_out, A2, not_4_out);
  and and_5 (and_5_out, not_5_out, B1);
  and and_6 (and_6_out, A1, not_6_out);
  and and_7 (and_7_out, not_7_out, B0);
  and and_8 (and_8_out, A0, not_8_out);
  nor nor_1 (nor_1_out, and_1_out, and_2_out);
  nor nor_2 (nor_2_out, and_3_out, and_4_out);
  nor nor_3 (nor_3_out, and_5_out, and_6_out);
  nor nor_4 (nor_4_out, and_7_out, and_8_out);
  and and_9 (and_9_out, nor_1_out, and_3_out);
  and and_10 (and_10_out, nor_1_out, and_4_out);
  and and_11 (and_11_out, and_5_out, nor_2_out, nor_1_out);
  and and_12 (and_12_out, nor_2_out, nor_1_out, and_6_out);
  and and_13 (and_13_out, nor_3_out, nor_2_out, nor_1_out, and_7_out);
  and and_14 (and_14_out, nor_3_out, nor_2_out, nor_1_out, and_8_out);
  and and_15 (A_B_3, nor_1_out, nor_2_out, nor_3_out, nor_4_out);
  or or_1 (A_B, and_9_out, and_11_out, and_13_out, and_1_out);
  or or_2 (A_B_2, and_10_out, and_2_out, and_12_out, and_14_out);
endmodule

module _4x1_MUX (
  input  S1,
  input  S0,
  input  I0,
  input  I1,
  input  I2,
  input  I3,
  output O
);

  wire and_1_out, and_2_out, and_3_out, and_4_out, and_5_out, and_6_out, and_7_out, and_8_out, not_1_out,
       not_2_out, not_3_out, not_4_out, or_1_out, or_2_out;

  not not_1 (not_1_out, S1);
  not not_2 (not_2_out, S0);
  not not_3 (not_3_out, S1);
  not not_4 (not_4_out, S0);
  and and_1 (and_1_out, not_1_out, not_2_out);
  and and_2 (and_2_out, not_3_out, S0);
  and and_3 (and_3_out, S1, not_4_out);
  and and_4 (and_4_out, S1, S0);
  and and_5 (and_5_out, and_1_out, I0);
  and and_6 (and_6_out, and_2_out, I1);
  and and_7 (and_7_out, and_3_out, I2);
  and and_8 (and_8_out, and_4_out, I3);
  or or_1 (or_1_out, and_5_out, and_6_out);
  or or_2 (or_2_out, and_7_out, and_8_out);
  or or_3 (O, or_1_out, or_2_out);
endmodule

module Subtractor (
  input  in_1,
  input  in_2,
  input  in_3,
  input  in_4,
  input  in_5,
  input  in_6,
  input  in_7,
  input  in_8,
  output A1,
  output A2,
  output A4,
  output A8
);

  wire adder_1_cout, adder_1_out, adder_2_cout, adder_2_out, adder_3_cout, adder_3_out, adder_4_out,
       adder_5_cout, adder_6_cout, adder_7_cout, n2x1_mux_1_o, n2x1_mux_2_o, n2x1_mux_3_o, n2x1_mux_4_o,
       not_1_out, not_2_out, not_3_out, not_4_out, not_5_out, not_6_out, not_7_out, not_8_out;

  not not_1 (not_1_out, in_2);
  not not_2 (not_2_out, in_4);
  not not_3 (not_3_out, in_6);
  not not_4 (not_4_out, in_8);
  Adder #(.width(1)) adder_1 (.a(in_1), .b(not_1_out), .out(adder_1_out), .cin(1'b1), .cout(adder_1_cout));
  Adder #(.width(1)) adder_2 (.a(in_3), .b(not_2_out), .out(adder_2_out), .cin(adder_1_cout), .cout(adder_2_cout));
  Adder #(.width(1)) adder_3 (.a(in_5), .b(not_3_out), .out(adder_3_out), .cin(adder_2_cout), .cout(adder_3_cout));
  Adder #(.width(1)) adder_4 (.a(in_7), .b(not_4_out), .out(adder_4_out), .cin(adder_3_cout));  // open: cout
  not not_5 (not_5_out, adder_1_out);
  not not_6 (not_6_out, adder_2_out);
  not not_7 (not_7_out, adder_3_out);
  not not_8 (not_8_out, adder_4_out);
  _2x1_MUX u_2x1_mux_1 (.S0(adder_4_out), .I0(adder_1_out), .I1(not_5_out), .O(n2x1_mux_1_o));
  _2x1_MUX u_2x1_mux_2 (.S0(adder_4_out), .I0(adder_2_out), .I1(not_6_out), .O(n2x1_mux_2_o));
  _2x1_MUX u_2x1_mux_3 (.S0(adder_4_out), .I0(adder_3_out), .I1(not_7_out), .O(n2x1_mux_3_o));
  _2x1_MUX u_2x1_mux_4 (.S0(adder_4_out), .I0(adder_4_out), .I1(not_8_out), .O(n2x1_mux_4_o));
  Adder #(.width(1)) adder_5 (.a(n2x1_mux_1_o), .b(1'b0), .out(A1), .cin(adder_4_out), .cout(adder_5_cout));
  Adder #(.width(1)) adder_6 (.a(n2x1_mux_2_o), .b(1'b0), .out(A2), .cin(adder_5_cout), .cout(adder_6_cout));
  Adder #(.width(1)) adder_7 (.a(n2x1_mux_3_o), .b(1'b0), .out(A4), .cin(adder_6_cout), .cout(adder_7_cout));
  Adder #(.width(1)) adder_8 (.a(n2x1_mux_4_o), .b(1'b0), .out(A8), .cin(adder_7_cout));  // open: cout

  // Notes on the sheet:
  //   A1
  //   A2
  //   A4
  //   A8
endmodule

module _2_to_4_Decoder (
  input  S1,
  input  S0,
  output D0,
  output D1,
  output D2,
  output D3
);

  wire not_1_out, not_2_out, not_3_out, not_4_out;

  not not_1 (not_1_out, S1);
  not not_2 (not_2_out, S0);
  not not_3 (not_3_out, S1);
  not not_4 (not_4_out, S0);
  and and_1 (D3, S1, S0);
  and and_2 (D0, not_1_out, not_2_out);
  and and_3 (D1, not_3_out, S0);
  and and_4 (D2, S1, not_4_out);
endmodule

module _2_bit_counter (
  output out_1,
  output out_2,
  output out_3
);

  wire not_1_out, xor_1_out;

  Clock clock_1 (.out(out_1));
  D_Flip_Flop d_ff_1 (.clk(out_1), .D(not_1_out), .Q(out_2));  // open: Qn, preset, en, reset
  D_Flip_Flop d_ff_2 (.clk(out_1), .D(xor_1_out), .Q(out_3));  // open: Qn, preset, en, reset
  not not_1 (not_1_out, out_2);
  xor xor_1 (xor_1_out, out_3, out_2);
endmodule
