// Logisim project Multipilcation.circ as structural Verilog: 2 circuits, main circuit main
module main (
  input  A0,
  input  A1,
  input  A2,
  input  A3,
  input  B3,
  input  A0_2,
  input  A1_2,
  input  A2_2,
  input  A3_2,
  input  B3_2,
  input  B0,
  input  B0_2,
  input  in_13,
  input  B0_3,
  input  in_15,
  input  B0_4,
  input  B1,
  input  B1_2,
  input  in_19,
  input  B0_5,
  input  in_21,
  input  B1_3,
  input  B0_6,
  input  B1_4,
  input  B2,
  input  B2_2,
  input  B1_5,
  input  B2_3,
  input  B1_6,
  input  B2_4,
  input  in_31,
  input  in_32,
  input  B1_7,
  input  B1_8,
  input  in_35,
  output C0,
  output C0_2,
  output C1,
  output C1_2,
  output C2,
  output C2_2,
  output C3,
  output C3_2,
  output out_44,
  output OVERFLOW,
  output out_46,
  output out_47
);

  wire adder_1_cout, adder_2_cout, adder_2_out, adder_3_cout, adder_3_out, adder_4_cout, adder_5_cout,
       adder_7_cout, adder_8_cout, adder_8_out, adder_9_out, adder_10_cout, adder_11_cout, adder_11_out,
       adder_12_out, and_2_out, and_3_out, and_4_out, and_5_out, and_6_out, and_7_out, and_8_out, and_9_out,
       and_11_out, and_12_out, and_13_out, and_14_out, and_15_out, and_16_out, and_17_out, and_18_out;

  and and_1 (C0, B0, A0);
  and and_2 (and_2_out, B1, A0);
  and and_3 (and_3_out, B2, A0);
  and and_4 (and_4_out, B0_3, A1);
  and and_5 (and_5_out, B1_3, A1);
  and and_6 (and_6_out, B2_3, A1);
  Adder #(.width(1)) adder_1 (.a(and_4_out), .b(and_2_out), .out(C1), .cin(in_13), .cout(adder_1_cout));
  Adder #(.width(1)) adder_2 (.a(and_5_out), .b(and_3_out), .out(adder_2_out), .cin(adder_1_cout), .cout(adder_2_cout));
  Adder #(.width(1)) adder_3 (.a(and_6_out), .b(in_31), .out(adder_3_out), .cin(adder_2_cout), .cout(adder_3_cout));
  and and_7 (and_7_out, B0_5, A2);
  and and_8 (and_8_out, B1_5, A2);
  and and_9 (and_9_out, B1_7, A2);
  Adder #(.width(1)) adder_4 (.a(and_7_out), .b(adder_2_out), .out(C2), .cin(in_19), .cout(adder_4_cout));
  Adder #(.width(1)) adder_5 (.a(and_8_out), .b(adder_3_out), .out(out_44), .cin(adder_4_cout), .cout(adder_5_cout));
  Adder #(.width(1)) adder_6 (.a(and_9_out), .b(adder_3_cout), .out(out_46), .cin(adder_5_cout), .cout(out_47));
  xor xor_1 (C3, A3, B3);
  and and_10 (C0_2, B0_2, A0_2);
  and and_11 (and_11_out, B1_2, A0_2);
  and and_12 (and_12_out, B2_2, A0_2);
  and and_13 (and_13_out, B0_4, A1_2);
  and and_14 (and_14_out, B1_4, A1_2);
  and and_15 (and_15_out, B2_4, A1_2);
  Adder #(.width(1)) adder_7 (.a(and_13_out), .b(and_11_out), .out(C1_2), .cin(in_15), .cout(adder_7_cout));
  Adder #(.width(1)) adder_8 (
    .a(and_14_out), .b(and_12_out), .out(adder_8_out), .cin(adder_7_cout), .cout(adder_8_cout));
  Adder #(.width(1)) adder_9 (.a(and_15_out), .b(in_32), .out(adder_9_out), .cin(adder_8_cout));  // open: cout
  and and_16 (and_16_out, B0_6, A2_2);
  and and_17 (and_17_out, B1_6, A2_2);
  and and_18 (and_18_out, B1_8, A2_2);
  Adder #(.width(1)) adder_10 (.a(and_16_out), .b(adder_8_out), .out(C2_2), .cin(in_21), .cout(adder_10_cout));
  Adder #(.width(1)) adder_11 (
    .a(and_17_out), .b(adder_9_out), .out(adder_11_out), .cin(adder_10_cout), .cout(adder_11_cout));
  Adder #(.width(1)) adder_12 (.a(and_18_out), .b(in_35), .out(adder_12_out), .cin(adder_11_cout));  // open: cout
  xor xor_2 (C3_2, A3_2, B3_2);
  or or_1 (OVERFLOW, adder_11_out, adder_12_out);
endmodule

module adder_circuit (
  input  Cin,
  input  A0,
  input  B0,
  input  A1,
  input  B1,
  input  A2,
  input  B2,
  input  A3,
  input  B3,
  output S0,
  output S1,
  output S2,
  output S3,
  output Cout
);

  wire adder_1_cout, adder_2_cout, adder_3_cout;

  Adder #(.width(1)) adder_1 (.a(A0), .b(B0), .out(S0), .cin(Cin), .cout(adder_1_cout));
  Adder #(.width(1)) adder_2 (.a(A1), .b(B1), .out(S1), .cin(adder_1_cout), .cout(adder_2_cout));
  Adder #(.width(1)) adder_3 (.a(A2), .b(B2), .out(S2), .cin(adder_2_cout), .cout(adder_3_cout));
  Adder #(.width(1)) adder_4 (.a(A3), .b(B3), .out(S3), .cin(adder_3_cout), .cout(Cout));
endmodule
