// Logisim project BCD MULTI.circ as structural Verilog: 1 circuit, main circuit main
module main (
  input  A3,
  input  A2,
  input  A1,
  input  A0,
  input  B3,
  input  B2,
  input  B1,
  input  B0
);

  wire adder_1_cout, adder_1_out, adder_2_cout, adder_2_out, adder_3_cout, adder_3_out, adder_4_cout,
       adder_4_out, adder_5_cout, adder_5_out, and_1_out, and_2_out, and_3_out, and_4_out, and_5_out,
       and_6_out, and_7_out, and_8_out, and_9_out, and_10_out, and_11_out, and_12_out, main_1_c0, main_1_c1,
       main_1_c2, main_1_c3, main_1_out_13, main_1_out_14, main_1_out_15, n7_segment_display_driver_1_p5,
       n7_segment_display_driver_1_p6, n7_segment_display_driver_1_p7, n7_segment_display_driver_1_p8,
       n7_segment_display_driver_1_p9, n7_segment_display_driver_1_p10, n7_segment_display_driver_1_p11,
       n7_segment_display_driver_2_p5, n7_segment_display_driver_2_p6, n7_segment_display_driver_2_p7,
       n7_segment_display_driver_2_p8, n7_segment_display_driver_2_p9, n7_segment_display_driver_2_p10,
       n7_segment_display_driver_2_p11, not_1_out, not_2_out, not_3_out, not_4_out, not_5_out, not_6_out,
       not_7_out, not_8_out, not_9_out, not_10_out, not_11_out, not_12_out, or_1_out, or_2_out, or_3_out,
       or_4_out, or_5_out, or_6_out, or_7_out;

  nnnnnnnn_main main_1 (
    .B0(B0), .B1(B1), .B2(B2), .C0(main_1_c0), .C1(main_1_c1), .C2(main_1_c2), .C3(main_1_c3),
    .out_13(main_1_out_13), .out_14(main_1_out_14), .out_15(main_1_out_15), .A0(A0), .A1(A1), .A2(A2),
    .A3(A3), .B3(B3));
  not not_1 (not_1_out, main_1_c1);
  not not_2 (not_2_out, main_1_c2);
  not not_3 (not_3_out, main_1_out_13);
  not not_4 (not_4_out, main_1_out_14);
  not not_5 (not_5_out, main_1_out_15);
  and and_1 (and_1_out, main_1_c2, main_1_out_13, not_4_out, not_5_out);
  and and_2 (and_2_out, main_1_c1, main_1_out_13, not_4_out, not_5_out);
  and and_3 (and_3_out, not_2_out, not_3_out, main_1_out_14, not_5_out);
  and and_4 (and_4_out, main_1_out_13, main_1_out_14, main_1_out_15);
  not not_6 (not_6_out, and_4_out);
  and and_5 (and_5_out, main_1_out_13, main_1_out_15);
  not not_7 (not_7_out, and_5_out);
  and and_6 (and_6_out, main_1_out_13, main_1_out_14, main_1_c2, main_1_c1);
  or or_1 (or_1_out, and_1_out, and_2_out, and_3_out);
  not not_8 (not_8_out, or_1_out);
  not not_9 (not_9_out, and_6_out);
  and and_7 (and_7_out, not_8_out, not_9_out, main_1_out_14, not_5_out);
  not not_10 (not_10_out, and_7_out);
  or or_2 (or_2_out, and_6_out, main_1_out_15);
  not not_11 (not_11_out, and_8_out);
  and and_8 (and_8_out, main_1_out_14, main_1_out_15);
  and and_9 (and_9_out, main_1_out_13, not_4_out, main_1_out_15);
  and and_10 (and_10_out, not_1_out, not_2_out, not_3_out, main_1_out_14, main_1_out_15);
  and and_11 (and_11_out, not_10_out, or_2_out, not_11_out, not_6_out, not_7_out);
  not not_12 (not_12_out, and_11_out);
  or or_3 (or_3_out, and_9_out, and_10_out);
  and and_12 (and_12_out, not_12_out, or_3_out);
  or or_4 (or_4_out, or_1_out, and_11_out);
  or or_5 (or_5_out, or_1_out, and_7_out);
  or or_6 (or_6_out, and_12_out, and_7_out);
  or or_7 (or_7_out, and_11_out, and_12_out);
  Adder #(.width(1)) adder_1 (.a(main_1_c1), .b(or_4_out), .out(adder_1_out), .cin(1'b0), .cout(adder_1_cout));
  Adder #(.width(1)) adder_2 (.a(main_1_c2), .b(or_5_out), .out(adder_2_out), .cin(adder_1_cout), .cout(adder_2_cout));
  Adder #(.width(1)) adder_3 (
    .a(main_1_out_13), .b(or_6_out), .out(adder_3_out), .cin(adder_2_cout), .cout(adder_3_cout));
  Adder #(.width(1)) adder_4 (
    .a(main_1_out_14), .b(or_7_out), .out(adder_4_out), .cin(adder_3_cout), .cout(adder_4_cout));
  Adder #(.width(1)) adder_5 (.a(main_1_out_15), .b(1'b0), .out(adder_5_out), .cin(adder_4_cout), .cout(adder_5_cout));
  // _7_segment_display_driver 7_segment_display_driver_1: pin names not known; wires that end beside it: adder_3_out, adder_2_out, adder_1_out, main_1_c0, n7_segment_display_driver_1_p5, n7_segment_display_driver_1_p6, n7_segment_display_driver_1_p7, n7_segment_display_driver_1_p8, n7_segment_display_driver_1_p9, n7_segment_display_driver_1_p10, n7_segment_display_driver_1_p11
  // _7_segment_display_driver 7_segment_display_driver_2: pin names not known; wires that end beside it: 1'b0, adder_5_cout, adder_5_out, adder_4_out, n7_segment_display_driver_2_p5, n7_segment_display_driver_2_p6, n7_segment_display_driver_2_p7, n7_segment_display_driver_2_p8, n7_segment_display_driver_2_p9, n7_segment_display_driver_2_p10, n7_segment_display_driver_2_p11
  _7_Segment_Display u_7_segment_display_1 (.g(main_1_c3));  // open: f, a, b, e, d, c, dp
  _7_Segment_Display u_7_segment_display_2 (
    .g(n7_segment_display_driver_2_p11), .f(n7_segment_display_driver_2_p10),
    .a(n7_segment_display_driver_2_p5), .b(n7_segment_display_driver_2_p6),
    .e(n7_segment_display_driver_2_p9), .d(n7_segment_display_driver_2_p8), .c(n7_segment_display_driver_2_p7));  // open: dp
  _7_Segment_Display u_7_segment_display_3 (
    .g(n7_segment_display_driver_1_p11), .f(n7_segment_display_driver_1_p10),
    .a(n7_segment_display_driver_1_p5), .b(n7_segment_display_driver_1_p6),
    .e(n7_segment_display_driver_1_p9), .d(n7_segment_display_driver_1_p8), .c(n7_segment_display_driver_1_p7));  // open: dp
endmodule
