// Logisim project FINAL DIVISION 2.circ as structural Verilog: 1 circuit, main circuit main
module main (
  input  A4,
  input  A3,
  input  A2,
  input  A1,
  input  B4,
  input  B3,
  input  B2,
  input  B1,
  output out_9,
  output out_10,
  output out_11,
  output out_12
);

  wire n2x1_mux_1_o, n2x1_mux_2_o, n2x1_mux_3_o, n7483_4_bit_binary_full_adders_with_fast_carry_1_p4,
       n7483_4_bit_binary_full_adders_with_fast_carry_2_p4,
       n7483_4_bit_binary_full_adders_with_fast_carry_2_p13, not_1_out, not_2_out, not_3_out;

  not not_1 (not_1_out, B3);
  not not_2 (not_2_out, B2);
  not not_3 (not_3_out, B1);
  xor xor_1 (out_9, A4, B4);
  // _7483___4_bit_Binary_Full_Adders_with_Fast_Carry 7483_4_bit_binary_full_adders_with_fast_carry_1: pin names not known; wires that end beside it: 1'b0, 1'b0, out_10, n7483_4_bit_binary_full_adders_with_fast_carry_1_p4, 1'b0, 1'b1, not_1_out, 1'b0, 1'b1, not_3_out, A3, not_2_out, 1'b0
  _2x1_MUX u_2x1_mux_1 (
    .S0(out_10), .I0(A3), .I1(n7483_4_bit_binary_full_adders_with_fast_carry_1_p4), .O(n2x1_mux_1_o));
  // _7483___4_bit_Binary_Full_Adders_with_Fast_Carry 7483_4_bit_binary_full_adders_with_fast_carry_2: pin names not known; wires that end beside it: 1'b0, 1'b0, out_11, n7483_4_bit_binary_full_adders_with_fast_carry_2_p4, 1'b0, 1'b1, not_1_out, 1'b0, 1'b1, not_3_out, A2, not_2_out, n7483_4_bit_binary_full_adders_with_fast_carry_2_p13, n2x1_mux_1_o
  _2x1_MUX u_2x1_mux_2 (
    .S0(out_11), .I0(n2x1_mux_1_o), .I1(n7483_4_bit_binary_full_adders_with_fast_carry_2_p4), .O(n2x1_mux_2_o));
  _2x1_MUX u_2x1_mux_3 (
    .S0(out_11), .I0(A2), .I1(n7483_4_bit_binary_full_adders_with_fast_carry_2_p13), .O(n2x1_mux_3_o));
  // _7483___4_bit_Binary_Full_Adders_with_Fast_Carry 7483_4_bit_binary_full_adders_with_fast_carry_3: pin names not known; wires that end beside it: 1'b0, 1'b0, out_12, n2x1_mux_2_o, 1'b1, not_1_out, 1'b0, 1'b1, not_3_out, A1, not_2_out, n2x1_mux_3_o
endmodule
