// Logisim project FINAL.circ as structural Verilog: 1 circuit, main circuit main
module main (
  input  A4,
  input  A3,
  input  A2,
  input  A1,
  input  B4,
  input  B3,
  input  B2,
  input  B1,
  input  in_9,
  input  in_10
);

  wire main_1_p10, main_1_p11, main_1_p12, main_1_p13, main_2__1, main_2__2, main_2__4, main_2_sign,
       main_3_out_9, main_3_out_10, main_3_out_11, main_3_out_12, n4x1_mux_1_o, n4x1_mux_2_o, n4x1_mux_3_o,
       n4x1_mux_4_o, n7448_decoder_1_a, n7448_decoder_1_b, n7448_decoder_1_c, n7448_decoder_1_d,
       n7448_decoder_1_e, n7448_decoder_1_f, n7448_decoder_1_g;

  // Multipilcation_main main_1: pin names not known; wires that end beside it: B4, B4, A4, A3, A2, A1, B3, B2, B1, main_1_p10, main_1_p11, main_1_p12, main_1_p13
  ADDERSUBTRACTORFinal_main main_2 (
    .A4(A4), .A3(A3), .A2(A2), .A1(A1), .B4(B4), .B3(B3), .B2(B2), .B1(B1), .SIGN(main_2_sign),
    ._4(main_2__4), ._2(main_2__2), ._1(main_2__1));  // open: Overflow
  FINAL_DIVISION_2_main main_3 (
    .A4(A4), .A3(A3), .A2(A2), .A1(A1), .B4(B4), .B3(B3), .B2(B2), .B1(B1), .out_9(main_3_out_9),
    .out_10(main_3_out_10), .out_11(main_3_out_11), .out_12(main_3_out_12));
  _4x1_MUX u_4x1_mux_1 (
    .S1(in_9), .S0(in_10), .I0(main_2_sign), .I1(main_2_sign), .I2(main_1_p13), .I3(main_3_out_9),
    .O(n4x1_mux_1_o));
  _4x1_MUX u_4x1_mux_2 (
    .S1(in_9), .S0(in_10), .I0(main_2__4), .I1(main_2__4), .I2(main_1_p12), .I3(main_3_out_10),
    .O(n4x1_mux_2_o));
  _4x1_MUX u_4x1_mux_3 (
    .S1(in_9), .S0(in_10), .I0(main_2__2), .I1(main_2__2), .I2(main_1_p11), .I3(main_3_out_11),
    .O(n4x1_mux_3_o));
  _4x1_MUX u_4x1_mux_4 (
    .S1(in_9), .S0(in_10), .I0(main_2__1), .I1(main_2__1), .I2(main_1_p10), .I3(main_3_out_12),
    .O(n4x1_mux_4_o));
  _7448_decoder u_7448_decoder_1 (
    .X(1'b0), .Y(n4x1_mux_2_o), .Z(n4x1_mux_3_o), .W(n4x1_mux_4_o), .a(n7448_decoder_1_a),
    .b(n7448_decoder_1_b), .c(n7448_decoder_1_c), .d(n7448_decoder_1_d), .e(n7448_decoder_1_e),
    .f(n7448_decoder_1_f), .g(n7448_decoder_1_g));
  _7_Segment_Display u_7_segment_display_1 (.g(n4x1_mux_1_o));  // open: f, a, b, e, d, c, dp
  _7_Segment_Display u_7_segment_display_2 (
    .g(n7448_decoder_1_g), .f(n7448_decoder_1_f), .a(n7448_decoder_1_a), .b(n7448_decoder_1_b),
    .e(n7448_decoder_1_e), .d(n7448_decoder_1_d), .c(n7448_decoder_1_c));  // open: dp
endmodule
