// Logisim project nnnnnnnn.circ as structural Verilog: 2 circuits, main circuit main
module main (
  input  A0,
  input  A1,
  input  A2,
  input  A3,
  input  B3,
  input  B0,
  input  B1,
  input  B2,
  output C0,
  output C1,
  output C2,
  output C3,
  output out_13,
  output out_14,
  output out_15
);

  wire adder_1_cout, adder_2_cout, adder_2_out, adder_3_cout, adder_3_out, adder_4_cout, adder_5_cout,
       and_2_out, and_3_out, and_4_out, and_5_out, and_6_out, and_7_out, and_8_out, and_9_out;

  and and_1 (C0, B0, A0);
  and and_2 (and_2_out, B1, A0);
  and and_3 (and_3_out, B2, A0);
  and and_4 (and_4_out, B0, A1);
  and and_5 (and_5_out, B1, A1);
  and and_6 (and_6_out, B2, A1);
  Adder #(.width(1)) adder_1 (.a(and_4_out), .b(and_2_out), .out(C1), .cin(1'b0), .cout(adder_1_cout));
  Adder #(.width(1)) adder_2 (.a(and_5_out), .b(and_3_out), .out(adder_2_out), .cin(adder_1_cout), .cout(adder_2_cout));
  Adder #(.width(1)) adder_3 (.a(and_6_out), .b(1'b0), .out(adder_3_out), .cin(adder_2_cout), .cout(adder_3_cout));
  and and_7 (and_7_out, B0, A2);
  and and_8 (and_8_out, B1, A2);
  and and_9 (and_9_out, B2, A2);
  Adder #(.width(1)) adder_4 (.a(and_7_out), .b(adder_2_out), .out(C2), .cin(1'b0), .cout(adder_4_cout));
  Adder #(.width(1)) adder_5 (.a(and_8_out), .b(adder_3_out), .out(out_13), .cin(adder_4_cout), .cout(adder_5_cout));
  Adder #(.width(1)) adder_6 (.a(and_9_out), .b(adder_3_cout), .out(out_14), .cin(adder_5_cout), .cout(out_15));
  xor xor_1 (C3, A3, B3);
endmodule

module adder_circuit (
  input  Cin,
  input  A0,
  input  B0,
  input  A1,
  input  B1,
  input  A2,
  input  B2,
  input  A3,
  input  B3,
  output S0,
  output S1,
  output S2,
  output S3,
  output Cout
);

  wire adder_1_cout, adder_2_cout, adder_3_cout;

  Adder #(.width(1)) adder_1 (.a(A0), .b(B0), .out(S0), .cin(Cin), .cout(adder_1_cout));
  Adder #(.width(1)) adder_2 (.a(A1), .b(B1), .out(S1), .cin(adder_1_cout), .cout(adder_2_cout));
  Adder #(.width(1)) adder_3 (.a(A2), .b(B2), .out(S2), .cin(adder_2_cout), .cout(adder_3_cout));
  Adder #(.width(1)) adder_4 (.a(A3), .b(B3), .out(S3), .cin(adder_3_cout), .cout(Cout));
endmodule
